// Logisim project 4bitmicro.circ as structural Verilog: 6 circuits, main circuit main
module CPU (
  input  CLK,
  input  [7:0] DATAi,
  input  RESET,
  output [7:0] DATAo,
  output [11:0] ADDRESS,
  output MEMRD,
  output MEMWR
);

  wire and_1_out, and_2_out, CLK_t, CRST, Fc, Feq, IFCR, IFEQ, not_1_out, not_2_out, or_1_out, or_2_out;
  wire [2:0] XFER;
  wire [3:0] alu_1_dout, mem_1_datao, mem_1_inst;
  wire [4:0] INST_ROM_data;
  wire [6:0] ADDRi, ALUi;
  wire [7:0] Mar;
  wire [10:0] MEMi;

  ROM #(.dataWidth(5)) INST_ROM (.addr(Mar), .data(INST_ROM_data));
  not not_1 (not_1_out, CLK);
  buf buffer_1 (CLK_t, CLK);
  MEM mem_1 (
    .WIDEi(DATAi), .DATAi(alu_1_dout), .WIDEie(MEMi[0]), .DATAie(MEMi[1]), .Dll(MEMi[2]), .Dhl(MEMi[3]),
    .ARl(MEMi[4]), .IRl(MEMi[5]), .Dlo(MEMi[6]), .Dho(MEMi[7]), .ARo(MEMi[8]), .WIDEoe(MEMi[9]),
    .DATAoe(MEMi[10]), .RST(RESET), .CLK(CLK_t), .WIDEo(DATAo), .DATAo(mem_1_datao), .INST(mem_1_inst));
  not not_2 (not_2_out, Fc);
  and and_1 (and_1_out, not_2_out, IFCR);
  and and_2 (and_2_out, Feq, IFEQ);
  or or_1 (or_1_out, and_1_out, and_2_out, ADDRi[1]);
  or or_2 (or_2_out, and_1_out, and_2_out, ADDRi[0]);
  ALU alu_1 (
    .Din(mem_1_datao), .Ae(ALUi[0]), .Be(ALUi[1]), .Ce(ALUi[2]), .De(ALUi[3]), .Se(ALUi[4]), .Fe(ALUi[5]),
    .ALUe(ALUi[6]), .CLK(CLK_t), .RST(RESET), .XFER(XFER), .Dout(alu_1_dout), .Fc(Fc), .Feq(Feq));
  INST_DEC inst_dec_1 (.INST(mem_1_inst), .CRST(CRST), .CLK(not_1_out), .RESET(RESET), .INSTOUT(Mar));
  ADDR addr_1 (
    .Win(DATAo), .Din(alu_1_dout), .ILl(or_2_out), .IHl(or_1_out), .PLl(ADDRi[2]), .PHl(ADDRi[3]),
    .Io(ADDRi[4]), .Po(ADDRi[5]), .PPP(ADDRi[6]), .CLK(CLK_t), .RST(RESET), .Ax(ADDRESS));
  ROM #(.addrWidth(5), .dataWidth(32)) INST_DECODER (
    .addr(INST_ROM_data), .data({XFER[1:0], CRST, MEMWR, MEMRD, IFCR, IFEQ, ADDRi, MEMi, ALUi}));
  ROM #(.addrWidth(5), .dataWidth(1)) rom_1 (.addr(INST_ROM_data));  // open: data

  // Other names for the same wires on the sheet: Ax[11:0] = ADDRESS; RST = RESET

  // Notes on the sheet:
  //   contents of INST_ROM (hex, n*v repeats v):
  //   19 0 15 c 18 11*0 19 0 15 c 7 3 18 9*0 19 0 15 c 0 6 15 d 17 2 16 18 4*0 19 0 15 c 0 6 15 d 17 9 16
  //   18 4*0 19 0 15 c 4 18 10*0 19 0 15 c 5 18 10*0 19 0 15 c 0 6 15 d 17 e 18 5*0 19 0 15 c 0 6 15 d 17
  //   f 18 5*0 19 0 15 c 0 6 15 d 13 18 6*0 19 0 15 c 0 6 15 d 14 18 6*0 19 0 15 c a 18 10*0 19 0 15 c 2 8
  //   f 18 8*0 19 0 15 c 2 11 10 18 8*0 19 0 15 c 9 12 10 18 8*0 19 0 15 c 0 6 15 d 17 b 18 5*0 19 0 15 c
  //   0 6 15 d 17 1 16 18
  //   contents of INST_DECODER (hex, n*v repeats v):
  //   1000000 40000508 40000308 64 40028001 40028002 40128008 40028010 80000001 80000308 c0000002 40024001
  //   1800 210000 40022001 40022002 40022020 1 2 4800000 2800000 8400680 10810000 8800680 20000000
  //   contents of rom_1 (hex, n*v repeats v):
  //   4*0 4*1 0 0 0 1 0 0 5*1
endmodule

module ALU (
  input  [3:0] Din,
  input  Ae,
  input  Be,
  input  Ce,
  input  De,
  input  Se,
  input  Fe,
  input  ALUe,
  input  CLK,
  input  RST,
  input  [2:0] XFER,
  output [3:0] Dout,
  output Fc,
  output Feq
);

  wire Fi, Fm, XFERA, XFERB, XFERC, XFERD, XFERF;
  wire [2:1] tialu_1_co;
  wire [3:0] A_q, B_q, C_q, DB, S_q, tialu_1_f;

  assign DB = XFERD ? Din : 4'bz;  // Controlled_Buffer controlled_buffer_1
  Decoder #(.select(3)) decoder_1 (
    .out1(XFERA), .out2(XFERB), .out3(XFERC), .out4(XFERF), .out5(XFERD), .sel(XFER));  // open: out0, out6, out7, en
  Register #(.width(4)) A (.D(DB), .en(Ae), .clk(CLK), .Q(A_q), .clr(RST));
  Register #(.width(4)) B (.D(DB), .en(Be), .clk(CLK), .Q(B_q), .clr(RST));
  Register #(.width(4)) S (.D(DB), .en(Se), .clk(CLK), .Q(S_q), .clr(RST));
  assign DB = XFERA ? A_q : 4'bz;  // Controlled_Buffer controlled_buffer_2
  assign DB = XFERB ? B_q : 4'bz;  // Controlled_Buffer controlled_buffer_3
  Register #(.width(4)) C (.D(tialu_1_f), .en(Ce), .clk(CLK), .Q(C_q), .clr(RST));
  TIALU tialu_1 (
    .M(Fm), .Cn(Fc), .Co(tialu_1_co[1]), .AeqB(tialu_1_co[2]), .A(A_q), .B(B_q), .S(S_q), .F(tialu_1_f));  // open: Y, X
  Register #(.width(4)) F (.D(DB), .en(Fe), .clk(CLK), .Q({Fm, Feq, Fc, Fi}), .clr(RST));
  assign DB = ALUe ? {Fm, tialu_1_co, Fi} : 4'bz;  // Controlled_Buffer controlled_buffer_4
  assign DB = XFERF ? {Fm, Feq, Fc, Fi} : 4'bz;  // Controlled_Buffer controlled_buffer_5
  assign DB = XFERC ? C_q : 4'bz;  // Controlled_Buffer controlled_buffer_6
  assign Dout = De ? DB : 4'bz;  // Controlled_Buffer controlled_buffer_7
endmodule

module ADDR (
  input  [7:0] Win,
  input  [3:0] Din,
  input  ILl,
  input  IHl,
  input  PLl,
  input  PHl,
  input  Io,
  input  Po,
  input  PPP,
  input  CLK,
  input  RST,
  output [11:0] Ax
);

  wire and_1_out, and_2_out, IL_carry;
  wire [3:0] IL_q, PL_q;
  wire [7:0] IH_q, PH_q;

  and and_1 (and_1_out, ILl, IHl, Po);
  Counter #(.width(4), .max('hf)) IL (
    .clr(RST), .load(ILl), .count(PPP), .clk(CLK), .D(Din), .carry(IL_carry), .Q(IL_q));  // open: up
  Register #(.width(4)) PL (.D(Din), .en(PLl), .clk(CLK), .Q(PL_q), .clr(RST));
  assign Ax[3:0] = Po ? PL_q : 4'bz;  // Controlled_Buffer controlled_buffer_1
  assign Ax[3:0] = Io ? IL_q : 4'bz;  // Controlled_Buffer controlled_buffer_2
  assign Din = and_1_out ? Ax[3:0] : 4'bz;  // Controlled_Buffer controlled_buffer_3
  Register PH (.D(Win), .en(PHl), .clk(CLK), .Q(PH_q), .clr(RST));
  and and_2 (and_2_out, PPP, IL_carry);
  Counter IH (.clr(RST), .load(IHl), .count(and_2_out), .clk(CLK), .D(Win), .Q(IH_q));  // open: up, carry
  assign Ax[11:4] = Po ? PH_q : 8'bz;  // Controlled_Buffer controlled_buffer_4
  assign Win = and_1_out ? Ax[11:4] : 8'bz;  // Controlled_Buffer controlled_buffer_5
  assign Ax[11:4] = Io ? IH_q : 8'bz;  // Controlled_Buffer controlled_buffer_6

  // Other names for the same wires on the sheet: DATA[3:0] = Din; WIDE[7:0] = Win
endmodule

module MEM (
  input  [7:0] WIDEi,
  input  [3:0] DATAi,
  input  WIDEie,
  input  DATAie,
  input  Dll,
  input  Dhl,
  input  ARl,
  input  IRl,
  input  Dlo,
  input  Dho,
  input  ARo,
  input  WIDEoe,
  input  DATAoe,
  input  RST,
  input  CLK,
  output [7:0] WIDEo,
  output [3:0] DATAo,
  output [3:0] INST
);

  wire and_1_out, buffer_1_out, not_1_out;
  wire [3:0] AR_q, controlled_buffer_5_out;
  wire [7:0] controlled_buffer_1_out, WIDEio;

  assign controlled_buffer_1_out = buffer_1_out ? WIDEi : 8'bz;  // Controlled_Buffer controlled_buffer_1
  buf buffer_1 (buffer_1_out, WIDEie);
  assign controlled_buffer_1_out = and_1_out ? WIDEio : 8'bz;  // Controlled_Buffer controlled_buffer_2
  and and_1 (and_1_out, ~DATAie, not_1_out);  // AND_Gate
  not not_1 (not_1_out, WIDEie);
  assign controlled_buffer_1_out[7:4] = DATAie ? DATAi : 4'bz;  // Controlled_Buffer controlled_buffer_3
  assign controlled_buffer_1_out[3:0] = DATAie ? DATAi : 4'bz;  // Controlled_Buffer controlled_buffer_4
  Register #(.width(4)) Dl (.D(controlled_buffer_1_out[3:0]), .en(Dll), .clk(CLK), .Q(WIDEio[3:0]), .clr(RST));
  Register #(.width(4)) Dh (.D(controlled_buffer_1_out[7:4]), .en(Dhl), .clk(CLK), .Q(WIDEio[7:4]), .clr(RST));
  assign controlled_buffer_5_out = Dlo ? WIDEio[3:0] : 4'bz;  // Controlled_Buffer controlled_buffer_5
  assign controlled_buffer_5_out = Dho ? WIDEio[7:4] : 4'bz;  // Controlled_Buffer controlled_buffer_6
  Register #(.width(4)) AR (.D(controlled_buffer_1_out[3:0]), .en(ARl), .clk(CLK), .Q(AR_q), .clr(RST));
  Register #(.width(4)) IR (.D(controlled_buffer_1_out[7:4]), .en(IRl), .clk(CLK), .Q(INST), .clr(RST));
  assign WIDEo = WIDEoe ? WIDEio : 8'bz;  // Controlled_Buffer controlled_buffer_7
  assign DATAo = DATAoe ? controlled_buffer_5_out : 4'bz;  // Controlled_Buffer controlled_buffer_8
  assign controlled_buffer_5_out = ARo ? AR_q : 4'bz;  // Controlled_Buffer controlled_buffer_9

  // Other names for the same wires on the sheet: DATA[3:0] = DATAi; WIDE[7:0] = WIDEi
endmodule

module INST_DEC (
  input  [3:0] INST,
  input  CRST,
  input  CLK,
  input  RESET,
  output [7:0] INSTOUT
);

  wire and_1_out, buffer_1_out, buffer_2_out, or_1_out;

  and and_1 (and_1_out, CRST, ~CLK);  // AND_Gate
  Counter #(.width(4), .max('hf)) counter_1 (
    .clr(or_1_out), .clk(buffer_2_out), .Q(INSTOUT[3:0]));  // open: load, up, count, D, carry
  or or_1 (or_1_out, RESET, and_1_out);
  buf buffer_1 (buffer_1_out, CLK);
  buf buffer_2 (buffer_2_out, buffer_1_out);

  assign INSTOUT[7:4] = INST;
endmodule

module main (
);

  wire button_1_out, clock_1_out, comparator_1_eq, cpu_1_memrd, cpu_1_memwr, t_ff_1_q;
  wire [7:0] cpu_1_datao;
  wire [11:0] controlled_buffer_1_out, cpu_1_address;

  Clock clock_1 (.out(clock_1_out));
  Button button_1 (.out(button_1_out));
  assign controlled_buffer_1_out = cpu_1_memwr ? cpu_1_address : 12'bz;  // Controlled_Buffer controlled_buffer_1
  Pull_Resistor pull_resistor_1 (.node(controlled_buffer_1_out));
  CPU cpu_1 (
    .CLK(clock_1_out), .DATAi(cpu_1_datao), .RESET(button_1_out), .DATAo(cpu_1_datao),
    .ADDRESS(cpu_1_address), .MEMRD(cpu_1_memrd), .MEMWR(cpu_1_memwr));
  T_Flip_Flop t_ff_1 (.T(comparator_1_eq), .clk(comparator_1_eq), .Q(t_ff_1_q));  // open: Qn, reset, preset
  Comparator #(.width(12), .mode("unsigned")) comparator_1 (
    .a(12'hffe), .b(controlled_buffer_1_out), .eq(comparator_1_eq));  // open: gt, lt
  TTY #(.trigger("falling")) tty_1 (.data(cpu_1_datao[6:0]), .clk(t_ff_1_q));  // open: we, clr
  RAM #(.addrWidth(12), .trigger("high")) ram_1 (
    .addr(cpu_1_address), .we(cpu_1_memwr), .oe(cpu_1_memrd), .data(cpu_1_datao));
endmodule
