// Logisim project alu.circ as structural Verilog: 2 circuits, main circuit TIALU
// 74181
module TIALU (
  input  [3:0] S,
  input  [3:0] A,
  input  [3:0] B,
  input  M,
  input  Cn,
  output Y,
  output Co,
  output X,
  output AeqB,
  output [3:0] F
);

  wire and_1_out, and_2_out, and_3_out, and_4_out, and_5_out, and_6_out, and_7_out, and_8_out, and_9_out,
       and_10_out, and_11_out, and_12_out, and_13_out, and_14_out, and_15_out, and_16_out, and_17_out,
       and_18_out, and_19_out, and_20_out, and_21_out, and_22_out, and_23_out, and_24_out, and_25_out,
       and_26_out, and_27_out, and_28_out, buffer_1_out, buffer_2_out, buffer_3_out, buffer_4_out,
       buffer_5_out, nand_1_out, nand_3_out, nor_1_out, nor_2_out, nor_3_out, nor_4_out, nor_5_out,
       nor_6_out, nor_7_out, nor_8_out, nor_10_out, nor_11_out, nor_12_out, not_1_out, not_2_out, not_3_out,
       not_4_out, not_5_out, xor_1_out, xor_2_out, xor_3_out, xor_4_out;

  not not_1 (not_1_out, B[3]);
  not not_2 (not_2_out, B[2]);
  not not_3 (not_3_out, B[1]);
  not not_4 (not_4_out, B[0]);
  not not_5 (not_5_out, M);
  and and_1 (and_1_out, B[3], S[3], A[3]);
  nor nor_1 (nor_1_out, and_1_out, and_2_out);
  and and_2 (and_2_out, A[3], S[2], not_1_out);
  and and_3 (and_3_out, not_1_out, S[1]);
  nor nor_2 (nor_2_out, and_3_out, and_4_out, buffer_1_out);
  and and_4 (and_4_out, S[0], B[3]);
  buf buffer_1 (buffer_1_out, A[3]);
  and and_5 (and_5_out, B[2], S[3], A[2]);
  nor nor_3 (nor_3_out, and_5_out, and_6_out);
  and and_6 (and_6_out, A[2], S[2], not_2_out);
  and and_7 (and_7_out, not_2_out, S[1]);
  and and_8 (and_8_out, S[0], B[2]);
  nor nor_4 (nor_4_out, and_7_out, and_8_out, buffer_2_out);
  buf buffer_2 (buffer_2_out, A[2]);
  and and_9 (and_9_out, B[1], S[3], A[1]);
  nor nor_5 (nor_5_out, and_9_out, and_10_out);
  and and_10 (and_10_out, A[1], S[2], not_3_out);
  and and_11 (and_11_out, not_3_out, S[1]);
  nor nor_6 (nor_6_out, and_11_out, and_12_out, buffer_3_out);
  and and_12 (and_12_out, S[0], B[1]);
  buf buffer_3 (buffer_3_out, A[1]);
  and and_13 (and_13_out, B[0], S[3], A[0]);
  nor nor_7 (nor_7_out, and_13_out, and_14_out);
  and and_14 (and_14_out, A[0], S[2], not_4_out);
  and and_15 (and_15_out, not_4_out, S[1]);
  and and_16 (and_16_out, S[0], B[0]);
  nor nor_8 (nor_8_out, and_15_out, and_16_out, buffer_4_out);
  buf buffer_4 (buffer_4_out, A[0]);
  xor xor_1 (xor_1_out, nor_1_out, nor_2_out);
  xor xor_2 (xor_2_out, nor_3_out, nor_4_out);
  xor xor_3 (xor_3_out, nor_5_out, nor_6_out);
  xor xor_4 (xor_4_out, nor_7_out, nor_8_out);
  buf buffer_5 (buffer_5_out, nor_2_out);
  and and_17 (and_17_out, nor_1_out, nor_4_out);
  and and_18 (and_18_out, nor_1_out, nor_3_out, nor_6_out);
  and and_19 (and_19_out, nor_1_out, nor_3_out, nor_5_out, nor_8_out);
  nand nand_1 (nand_1_out, nor_1_out, nor_3_out, nor_5_out, nor_7_out, Cn);
  nand nand_2 (X, nor_1_out, nor_3_out, nor_5_out, nor_7_out);
  and and_20 (and_20_out, Cn, nor_7_out, nor_5_out, nor_3_out, not_5_out);
  and and_21 (and_21_out, nor_5_out, nor_3_out, nor_8_out, not_5_out);
  and and_22 (and_22_out, nor_3_out, nor_6_out, not_5_out);
  and and_23 (and_23_out, nor_4_out, not_5_out);
  and and_24 (and_24_out, Cn, nor_7_out, nor_5_out, not_5_out);
  and and_25 (and_25_out, nor_5_out, nor_8_out, not_5_out);
  and and_26 (and_26_out, nor_6_out, not_5_out);
  and and_27 (and_27_out, Cn, nor_7_out, not_5_out);
  and and_28 (and_28_out, nor_8_out, not_5_out);
  nand nand_3 (nand_3_out, Cn, not_5_out);
  nor nor_9 (Y, buffer_5_out, and_17_out, and_18_out, and_19_out);
  nor nor_10 (nor_10_out, and_20_out, and_21_out, and_22_out, and_23_out);
  nor nor_11 (nor_11_out, and_24_out, and_25_out, and_26_out);
  nor nor_12 (nor_12_out, and_27_out, and_28_out);
  or or_1 (Co, ~Y, ~nand_1_out);  // OR_Gate
  xor xor_5 (F[3], xor_1_out, nor_10_out);
  xor xor_6 (F[2], xor_2_out, nor_11_out);
  xor xor_7 (F[1], xor_3_out, nor_12_out);
  xor xor_8 (F[0], xor_4_out, nand_3_out);
  and and_29 (AeqB, F[3], F[2], F[1], F[0]);
endmodule

// 74182
module TICarryLookAhead (
  input  X3,
  input  Y3,
  input  X2,
  input  Y2,
  input  X1,
  input  Y1,
  input  X0,
  input  Y0,
  input  Cn,
  output X,
  output Y,
  output Coz,
  output Coy,
  output Cox
);

  wire and_1_out, and_2_out, and_3_out, and_4_out, and_5_out, and_6_out, and_7_out, and_8_out, and_9_out,
       and_10_out, and_11_out, and_12_out, and_13_out, not_1_out;

  not not_1 (not_1_out, Cn);
  or or_1 (X, X3, X2, X1, X0);
  and and_1 (and_1_out, Y3, Y2, Y1, Y0);
  and and_2 (and_2_out, X1, Y3, Y2, Y1);
  and and_3 (and_3_out, X2, Y3, Y2);
  and and_4 (and_4_out, X3, Y3);
  and and_5 (and_5_out, Y2, Y1, Y0, not_1_out);
  and and_6 (and_6_out, X0, Y2, Y1, Y0);
  and and_7 (and_7_out, X1, Y2, Y1);
  and and_8 (and_8_out, X2, Y2);
  and and_9 (and_9_out, Y1, Y0, not_1_out);
  and and_10 (and_10_out, X0, Y1, Y0);
  and and_11 (and_11_out, X1, Y1);
  and and_12 (and_12_out, Y0, not_1_out);
  and and_13 (and_13_out, X0, Y0);
  or or_2 (Y, and_1_out, and_2_out, and_3_out, and_4_out);
  nor nor_1 (Coz, and_5_out, and_6_out, and_7_out, and_8_out);
  nor nor_2 (Coy, and_9_out, and_10_out, and_11_out);
  nor nor_3 (Cox, and_12_out, and_13_out);
endmodule
