// Logisim project RISC32.circ as structural Verilog: 10 circuits, main circuit main
module main (
);

  wire button_1_out, button_2_out, clock_1_out, cpu_1_io_read, cpu_1_io_write, not_1_out, RD, WR;
  wire [15:0] bit_extender_1_out;
  wire [31:0] ADDR, controlled_buffer_3_out, cpu_1_io_data, Mem_I, Mem_O, ram_1_data, register_1_q;

  Bit_Extender #(.in_width(32), .\type ("zero")) bit_extender_1 (.in(ADDR), .out(bit_extender_1_out));
  RAM #(.addrWidth(16), .dataWidth(32), .trigger("high")) ram_1 (
    .addr(bit_extender_1_out), .we(WR), .oe(RD), .data(ram_1_data));
  assign Mem_I = RD ? ram_1_data : 32'bz;  // Controlled_Buffer controlled_buffer_1
  assign ram_1_data = WR ? Mem_O : 32'bz;  // Controlled_Buffer controlled_buffer_2
  Clock clock_1 (.out(clock_1_out));
  Button button_1 (.out(button_1_out));
  Button button_2 (.out(button_2_out));
  CPU cpu_1 (
    .Mem_I(Mem_I), .Clk(clock_1_out), .Reset(button_1_out), .IO_I(controlled_buffer_3_out),
    .INT(button_2_out), .Mem_O(Mem_O), .Addr(ADDR), .RD(RD), .WR(WR), .IO_Data(cpu_1_io_data),
    .IO_Write(cpu_1_io_write), .IO_Read(cpu_1_io_read));
  assign controlled_buffer_3_out = cpu_1_io_read ? register_1_q : 32'bz;  // Controlled_Buffer controlled_buffer_3
  Register #(.width(32)) register_1 (
    .D(cpu_1_io_data), .en(cpu_1_io_write), .clk(clock_1_out), .Q(register_1_q), .clr(button_1_out));
  Counter #(.width(32), .max('hffffffff), .trigger("falling")) counter_1 (
    .clr(button_1_out), .count(not_1_out), .clk(clock_1_out));  // open: load, up, D, carry, Q
  not not_1 (not_1_out, register_1_q[31]);
endmodule

module CPU (
  input  [31:0] Mem_I,
  input  Clk,
  input  Reset,
  input  [31:0] IO_I,
  input  INT,
  output [31:0] Mem_O,
  output [31:0] Addr,
  output RD,
  output WR,
  output [31:0] IO_Data,
  output IO_Write,
  output IO_Read
);

  wire and_1_out, EX_PC_Load, EX_Uninhibit, FE_RD, ID_Inhibit, MEM_Inhibit, MEM_RD, MEM_WR, or_1_out;
  wire [2:0] ex_1_inst_out;
  wire [3:0] ex_1_c_reg_out, WB_Reg;
  wire [31:0] ex_1_c_out, ex_1_f, ex_1_pc_out, EX_Addr, fe_1_ir, fe_1_pc, FE_Addr, id_1_a, id_1_b,
       id_1_c_dat, id_1_ir_out, id_1_pc_out, MEM_ADDR, WB_Data;

  or or_1 (or_1_out, Clk, Reset);
  FE fe_1 (
    .CLK(or_1_out), .Inhibit(ID_Inhibit), .Ld(EX_PC_Load), .Ld_Data(EX_Addr), .Mem_I(Mem_I), .Reset(Reset),
    .INT(INT), .RD(FE_RD), .ADDR(FE_Addr), .PC(fe_1_pc), .IR(fe_1_ir));
  Multiplexer #(.enable("false")) multiplexer_1 (.in0(FE_RD), .in1(MEM_RD), .out(RD), .sel(and_1_out));
  and and_1 (and_1_out, MEM_Inhibit, or_1_out);
  and and_2 (WR, MEM_WR, or_1_out);
  ID id_1 (
    .CLK(or_1_out), .WB_Reg(WB_Reg), .WB_Data(WB_Data), .Mem_Inhibit(MEM_Inhibit), .Uninhibit(EX_Uninhibit),
    .PC(fe_1_pc), .IR(fe_1_ir), .Reset(Reset), .IO_I(IO_I), .Inhibit(ID_Inhibit), .A(id_1_a), .B(id_1_b),
    .C_Dat(id_1_c_dat), .IR_Out(id_1_ir_out), .PC_Out(id_1_pc_out), .IO_O(IO_Data), .IO_WR(IO_Write),
    .IO_RD(IO_Read));
  Multiplexer #(.width(32), .enable("false")) multiplexer_2 (
    .in0(FE_Addr), .in1(MEM_ADDR), .out(Addr), .sel(MEM_Inhibit));
  EX ex_1 (
    .Clk(or_1_out), .A(id_1_a), .B(id_1_b), .C(id_1_c_dat), .IR(id_1_ir_out), .PC(id_1_pc_out),
    .WB_C(WB_Data), .Reset(Reset), .PC_ADDR(EX_Addr), .PC_Load(EX_PC_Load), .Uninhibit(EX_Uninhibit),
    .F(ex_1_f), .C_Out(ex_1_c_out), .C_Reg_Out(ex_1_c_reg_out), .INST_Out(ex_1_inst_out), .PC_Out(ex_1_pc_out));
  MEM mem_1 (
    .Clk(or_1_out), .F(ex_1_f), .C(ex_1_c_out), .C_Reg(ex_1_c_reg_out), .INST(ex_1_inst_out),
    .PC(ex_1_pc_out), .MEM_I(Mem_I), .Reset(Reset), .Inhibit(MEM_Inhibit), .RD(MEM_RD), .WR(MEM_WR),
    .ADDR(MEM_ADDR), .F_Out(WB_Data), .C_Reg_Out(WB_Reg), .MEM_O(Mem_O));

  // Other names for the same wires on the sheet: ID_IO[31:0] = IO_Data; ID_IORD = IO_Read; ID_IOWR = IO_Write
endmodule

module FE (
  input  CLK,
  input  Inhibit,
  input  Ld,
  input  [31:0] Ld_Data,
  input  [31:0] Mem_I,
  input  Reset,
  input  INT,
  output RD,
  output [31:0] ADDR,
  output [31:0] PC,
  output [31:0] IR
);

  wire and_1_out, buffer_1_out, buffer_2_out, buffer_3_out, buffer_4_out, buffer_5_out, buffer_6_out,
       buffer_7_out, buffer_8_out, buffer_9_out, buffer_10_out, buffer_11_out, buffer_12_out, button_1_out,
       comparator_1_eq, d_ff_1_q, Enable, or_1_out, or_2_out;
  wire [31:0] counter_1_q, multiplexer_2_out, multiplexer_3_out;

  Button button_1 (.out(button_1_out));
  not not_1 (Enable, Inhibit);
  buf buffer_1 (buffer_1_out, CLK);
  buf buffer_2 (buffer_2_out, buffer_1_out);
  buf buffer_3 (buffer_3_out, buffer_2_out);
  buf buffer_4 (buffer_4_out, buffer_3_out);
  buf buffer_5 (buffer_5_out, buffer_4_out);
  buf buffer_6 (buffer_6_out, buffer_5_out);
  buf buffer_7 (buffer_7_out, buffer_6_out);
  buf buffer_8 (buffer_8_out, buffer_7_out);
  buf buffer_9 (buffer_9_out, buffer_8_out);
  buf buffer_10 (buffer_10_out, buffer_9_out);
  buf buffer_11 (buffer_11_out, buffer_10_out);
  buf buffer_12 (buffer_12_out, buffer_11_out);
  or or_1 (or_1_out, INT, button_1_out);
  Counter #(.width(32), .max('hffffffff)) counter_1 (
    .clr(Reset), .load(Ld), .count(Enable), .clk(buffer_12_out), .D(Ld_Data), .Q(counter_1_q));  // open: up, carry
  and and_1 (and_1_out, CLK, Enable);
  D_Flip_Flop d_ff_1 (.D(1'b1), .clk(or_1_out), .Q(d_ff_1_q), .reset(or_2_out));  // open: Qn, preset
  and and_2 (RD, CLK, Enable);
  Multiplexer #(.width(32), .enable("false")) multiplexer_1 (
    .in1(counter_1_q), .out(ADDR), .sel(and_1_out));  // open: in0
  Register #(.width(32), .trigger("falling")) Program_Counter (
    .D(counter_1_q), .en(1'b1), .clk(CLK), .Q(PC), .clr(Reset));
  or or_2 (or_2_out, Reset, comparator_1_eq);
  Multiplexer #(.width(32), .enable("false")) multiplexer_2 (
    .in0(Mem_I), .in1(32'h9fe0e000), .out(multiplexer_2_out), .sel(d_ff_1_q));
  Multiplexer #(.width(32), .enable("false")) multiplexer_3 (
    .in0(multiplexer_2_out), .in1({32{1'b0}}), .out(multiplexer_3_out), .sel(Inhibit));
  Register #(.width(32), .trigger("falling")) register_1 (
    .D(multiplexer_3_out), .en(1'b1), .clk(CLK), .Q(IR), .clr(Reset));
  Comparator #(.width(32), .mode("unsigned")) comparator_1 (
    .a(IR), .b(32'h9fe0e000), .eq(comparator_1_eq));  // open: gt, lt
endmodule

module ID (
  input  CLK,
  input  [3:0] WB_Reg,
  input  [31:0] WB_Data,
  input  Mem_Inhibit,
  input  Uninhibit,
  input  [31:0] PC,
  input  [31:0] IR,
  input  Reset,
  input  [31:0] IO_I,
  output Inhibit,
  output [31:0] A,
  output [31:0] B,
  output [31:0] C_Dat,
  output [31:0] IR_Out,
  output [31:0] PC_Out,
  output [31:0] IO_O,
  output IO_WR,
  output IO_RD
);

  wire decoder_1_out4, decoder_1_out5, or_1_out, or_2_out, s_r_ff_1_q;
  wire [31:0] register_file_1_a, register_file_1_b, register_file_1_c;

  Decoder #(.select(3), .enable("false")) decoder_1 (
    .out4(decoder_1_out4), .out5(decoder_1_out5), .sel(IR[31:29]));  // open: out0, out1, out2, out3, out6, out7
  Register_File register_file_1 (
    .CLK(CLK), .A_Reg(IR[23:20]), .B_Reg(IR[19:16]), .Write_Reg(WB_Reg), .C_Reg(IR[15:12]), .Data(WB_Data),
    .Reset(Reset), .IO_I(IO_I), .A(register_file_1_a), .B(register_file_1_b), .C(register_file_1_c),
    .IO_O(IO_O), .IO_WR(IO_WR), .IO_RD(IO_RD));
  or or_1 (or_1_out, decoder_1_out4, decoder_1_out5);
  S_R_Flip_Flop s_r_ff_1 (.Q(s_r_ff_1_q), .reset(or_2_out), .preset(or_1_out));  // open: S, R, clk, Qn
  or or_2 (or_2_out, Reset, Uninhibit);
  or or_3 (Inhibit, s_r_ff_1_q, Mem_Inhibit);
  Register #(.width(32), .trigger("falling")) register_1 (
    .D(register_file_1_a), .en(1'b1), .clk(CLK), .Q(A), .clr(Reset));
  Register #(.width(32), .trigger("falling")) register_2 (
    .D(register_file_1_b), .en(1'b1), .clk(CLK), .Q(B), .clr(Reset));
  Register #(.width(32), .trigger("falling")) register_3 (
    .D(register_file_1_c), .en(1'b1), .clk(CLK), .Q(C_Dat), .clr(Reset));
  Register #(.width(32), .trigger("falling")) register_4 (.D(IR), .en(1'b1), .clk(CLK), .Q(IR_Out), .clr(Reset));
  Register #(.width(32), .trigger("falling")) register_5 (.D(PC), .en(1'b1), .clk(CLK), .Q(PC_Out), .clr(Reset));
endmodule

module Register_File (
  input  CLK,
  input  [3:0] A_Reg,
  input  [3:0] B_Reg,
  input  [3:0] Write_Reg,
  input  [3:0] C_Reg,
  input  [31:0] Data,
  input  Reset,
  input  [31:0] IO_I,
  output [31:0] A,
  output [31:0] B,
  output [31:0] C,
  output [31:0] IO_O,
  output IO_WR,
  output IO_RD
);

  wire and_1_out, and_2_out, and_3_out, wr1, wr2, wr3, wr4, wr5, wr6, wr7, wr8, wr9, wr10, wr11, wr12, wr13,
       wr14;
  wire [31:0] B_t, C_t, D, E, F, G, H, I, J, K, L, M, N, O;

  Decoder #(.select(4), .enable("false")) decoder_1 (
    .out1(wr1), .out2(wr2), .out3(wr3), .out4(wr4), .out5(wr5), .out6(wr6), .out7(wr7), .out8(wr8),
    .out9(wr9), .out10(wr10), .out11(wr11), .out12(wr12), .out13(wr13), .out14(wr14), .out15(IO_WR),
    .sel(Write_Reg));  // open: out0
  Register #(.width(32)) r1 (.D(Data), .en(wr1), .clk(CLK), .Q(B_t), .clr(Reset));
  Register #(.width(32)) r2 (.D(Data), .en(wr2), .clk(CLK), .Q(C_t), .clr(Reset));
  Register #(.width(32)) r3 (.D(Data), .en(wr3), .clk(CLK), .Q(D), .clr(Reset));
  Register #(.width(32)) r4 (.D(Data), .en(wr4), .clk(CLK), .Q(E), .clr(Reset));
  Register #(.width(32)) r5 (.D(Data), .en(wr5), .clk(CLK), .Q(F), .clr(Reset));
  Register #(.width(32)) r6 (.D(Data), .en(wr6), .clk(CLK), .Q(G), .clr(Reset));
  Register #(.width(32)) r7 (.D(Data), .en(wr7), .clk(CLK), .Q(H), .clr(Reset));
  Register #(.width(32)) r8 (.D(Data), .en(wr8), .clk(CLK), .Q(I), .clr(Reset));
  Register #(.width(32)) r9 (.D(Data), .en(wr9), .clk(CLK), .Q(J), .clr(Reset));
  Register #(.width(32)) r10 (.D(Data), .en(wr10), .clk(CLK), .Q(K), .clr(Reset));
  Register #(.width(32)) r11 (.D(Data), .en(wr11), .clk(CLK), .Q(L), .clr(Reset));
  Register #(.width(32)) r12 (.D(Data), .en(wr12), .clk(CLK), .Q(M), .clr(Reset));
  Register #(.width(32)) r13 (.D(Data), .en(wr13), .clk(CLK), .Q(N), .clr(Reset));
  Register #(.width(32)) r14 (.D(Data), .en(wr14), .clk(CLK), .Q(O), .clr(Reset));
  and and_1 (and_1_out, A_Reg[0], A_Reg[1], A_Reg[2], A_Reg[3]);
  and and_2 (and_2_out, B_Reg[0], B_Reg[1], B_Reg[2], B_Reg[3]);
  and and_3 (and_3_out, C_Reg[0], C_Reg[1], C_Reg[2], C_Reg[3]);
  or or_1 (IO_RD, and_1_out, and_2_out, and_3_out);
  Multiplexer #(.select(4), .width(32), .enable("false")) multiplexer_1 (
    .in0({32{1'b0}}), .in1(B_t), .in2(C_t), .in3(D), .in4(E), .in5(F), .in6(G), .in7(H), .in8(I), .in9(J),
    .in10(K), .in11(L), .in12(M), .in13(N), .in14(O), .in15(IO_I), .out(A), .sel(A_Reg));
  Multiplexer #(.select(4), .width(32), .enable("false")) multiplexer_2 (
    .in0({32{1'b0}}), .in1(B_t), .in2(C_t), .in3(D), .in4(E), .in5(F), .in6(G), .in7(H), .in8(I), .in9(J),
    .in10(K), .in11(L), .in12(M), .in13(N), .in14(O), .in15(IO_I), .out(B), .sel(B_Reg));
  Multiplexer #(.select(4), .width(32), .enable("false")) multiplexer_3 (
    .in0({32{1'b0}}), .in1(B_t), .in2(C_t), .in3(D), .in4(E), .in5(F), .in6(G), .in7(H), .in8(I), .in9(J),
    .in10(K), .in11(L), .in12(M), .in13(N), .in14(O), .in15(IO_I), .out(C), .sel(C_Reg));

  assign IO_O = Data;

  // Other names for the same wires on the sheet: Clock = CLK; P[31:0] = IO_I; RegA[3:0] = A_Reg; RegB[3:0] = B_Reg;
  //   RegC[3:0] = C_Reg; wr15 = IO_WR; Wr_Reg[3:0] = Write_Reg
endmodule

module EX (
  input  Clk,
  input  [31:0] A,
  input  [31:0] B,
  input  [31:0] C,
  input  [31:0] IR,
  input  [31:0] PC,
  input  [31:0] WB_C,
  input  Reset,
  output [31:0] PC_ADDR,
  output PC_Load,
  output Uninhibit,
  output [31:0] F,
  output [31:0] C_Out,
  output [3:0] C_Reg_Out,
  output [2:0] INST_Out,
  output [31:0] PC_Out
);

  wire ALUC, and_1_out, and_2_out, BEQ, bitselector_1_out, d_ff_1_q, JLR, LW, not_1_out, ROT, SW;
  wire [1:0] alu_1_eq;
  wire [2:0] decoder_2_out0;
  wire [3:0] multiplexer_2_out;
  wire [4:0] bit_extender_2_out, Func;
  wire [31:0] A_Lock, adder_1_out, alu_1_f, B_Lock, barrel_rotator_1_rot, bit_extender_1_out,
       multiplexer_4_out, or_1_out, pull_resistor_1_node;

  // Probe on IR
  assign or_1_out = B_Lock | pull_resistor_1_node;  // OR_Gate or_1, 32 bits wide
  Pull_Resistor pull_resistor_1 (.node(pull_resistor_1_node));
  assign pull_resistor_1_node = not_1_out ? bit_extender_1_out : 32'bz;  // Controlled_Buffer controlled_buffer_1
  not not_1 (not_1_out, BEQ);
  assign bit_extender_1_out = {{20{IR[11]}}, IR[11:0]};  // Bit_Extender bit_extender_1
  Decoder #(.select(3), .enable("false")) decoder_1 (
    .out1(ALUC), .out2(LW), .out3(SW), .out4(JLR), .out5(BEQ), .out6(ROT), .sel(IR[31:29]));  // open: out0, out7
  and and_1 (and_1_out, ALUC, Clk);
  ALU alu_1 (.A(A_Lock), .B(or_1_out), .S(Func), .CIn(d_ff_1_q), .F(alu_1_f), .C(alu_1_eq[1]), .EQ(alu_1_eq[0]));
  D_Flip_Flop d_ff_1 (.D(alu_1_eq[1]), .clk(and_1_out), .Q(d_ff_1_q), .preset(Reset));  // open: Qn, reset
  Bit_Extender #(.in_width(32), .out_width(5)) bit_extender_2 (.in(or_1_out), .out(bit_extender_2_out));
  Multiplexer #(.width(5), .enable("false")) multiplexer_1 (.in0(IR[28:24]), .in1(5'b00110), .out(Func), .sel(BEQ));
  Decoder #(.select(2), .enable("false")) decoder_2 (
    .out0(decoder_2_out0[0]), .out2(decoder_2_out0[1]), .out3(decoder_2_out0[2]), .sel(alu_1_eq));  // open: out1
  Pipeline_Interlock pipeline_interlock_1 (
    .A(A), .B(B), .Mem_C(F), .WB_C(WB_C), .A_Reg(IR[23:20]), .B_Reg(IR[19:16]), .Mem_C_Reg(C_Reg_Out),
    .CLK(Clk), .Reset(Reset), .A_Out(A_Lock), .B_Out(B_Lock));
  // Probe on alu_1_f
  Adder #(.width(32)) adder_1 (.a(PC), .b(bit_extender_1_out), .out(adder_1_out));  // open: cin, cout
  BitSelector #(.width(3)) bitselector_1 (.in(decoder_2_out0), .out(bitselector_1_out), .sel(IR[25:24]));
  Barrel_Rotator barrel_rotator_1 (.A(A_Lock), .B(bit_extender_2_out), .Rot(barrel_rotator_1_rot));
  and and_2 (and_2_out, bitselector_1_out, BEQ);
  or or_2 (Uninhibit, BEQ, JLR);
  or or_3 (PC_Load, and_2_out, JLR);
  Multiplexer #(.width(4), .enable("false")) multiplexer_2 (
    .in0(IR[15:12]), .in1(4'b0000), .out(multiplexer_2_out), .sel(SW));
  // Probe on PC
  Multiplexer #(.width(32), .enable("false")) multiplexer_3 (
    .in0(alu_1_f), .in1(adder_1_out), .out(PC_ADDR), .sel(BEQ));
  Register #(.width(32), .trigger("falling")) register_1 (
    .D(multiplexer_4_out), .en(1'b1), .clk(Clk), .Q(F), .clr(Reset));
  Multiplexer #(.width(32), .enable("false")) multiplexer_4 (
    .in0(alu_1_f), .in1(barrel_rotator_1_rot), .out(multiplexer_4_out), .sel(ROT));
  Register #(.width(32), .trigger("falling")) register_2 (.D(C), .en(1'b1), .clk(Clk), .Q(C_Out), .clr(Reset));
  Register #(.width(4), .trigger("falling")) register_3 (
    .D(multiplexer_2_out), .en(1'b1), .clk(Clk), .Q(C_Reg_Out), .clr(Reset));
  Register #(.width(3), .trigger("falling")) register_4 (
    .D(IR[31:29]), .en(1'b1), .clk(Clk), .Q(INST_Out), .clr(Reset));
  Register #(.width(32), .trigger("falling")) register_5 (.D(PC), .en(1'b1), .clk(Clk), .Q(PC_Out), .clr(Reset));

  // Other names for the same wires on the sheet: IMMD[11:0] = IR[11:0]; C_Reg[3:0] = IR[15:12];
  //   B_Reg[3:0] = IR[19:16]; A_Reg[3:0] = IR[23:20]; S[4:0] = IR[28:24]; INST[2:0] = IR[31:29]; Mem_C[31:0] = F;
  //   Mem_C_Reg[3:0] = C_Reg_Out
endmodule

module Barrel_Rotator (
  input  [31:0] A,
  input  [4:0] B,
  output [31:0] Rot
);

  wire [31:0] i0, i1, i2, i3;

  Multiplexer #(.width(32), .enable("false")) multiplexer_1 (.in0(A), .in1({A[30:0], A[31]}), .out(i0), .sel(B[0]));
  Multiplexer #(.width(32), .enable("false")) multiplexer_2 (
    .in0(i0), .in1({i0[29:0], i0[31:30]}), .out(i1), .sel(B[1]));
  Multiplexer #(.width(32), .enable("false")) multiplexer_3 (
    .in0(i1), .in1({i1[27:0], i1[31:28]}), .out(i2), .sel(B[2]));
  Multiplexer #(.width(32), .enable("false")) multiplexer_4 (
    .in0(i2), .in1({i2[23:0], i2[31:24]}), .out(i3), .sel(B[3]));
  Multiplexer #(.width(32), .enable("false")) multiplexer_5 (
    .in0(i3), .in1({i3[15:0], i3[31:16]}), .out(Rot), .sel(B[4]));
  // Probe on Rot

  // Other names for the same wires on the sheet: sA[31:0] = {A[30:0], A[31]}; sB[31:0] = {i0[29:0], i0[31:30]};
  //   sC[31:0] = {i1[27:0], i1[31:28]}; sD[31:0] = {i2[23:0], i2[31:24]}; sE[31:0] = {i3[15:0], i3[31:16]}
endmodule

module Pipeline_Interlock (
  input  [31:0] A,
  input  [31:0] B,
  input  [31:0] Mem_C,
  input  [31:0] WB_C,
  input  [3:0] A_Reg,
  input  [3:0] B_Reg,
  input  [3:0] Mem_C_Reg,
  input  CLK,
  input  Reset,
  output [31:0] A_Out,
  output [31:0] B_Out
);

  wire comparator_1_eq, comparator_2_eq, comparator_3_eq, comparator_4_eq, comparator_5_eq, comparator_6_eq,
       comparator_7_eq, comparator_8_eq, or_1_out, or_2_out;
  wire [1:0] and_1_out, and_2_out;
  wire [3:0] register_1_q;

  Register #(.width(4), .trigger("falling")) register_1 (
    .D(Mem_C_Reg), .en(1'b1), .clk(CLK), .Q(register_1_q), .clr(Reset));
  Multiplexer #(.select(2), .width(32), .enable("false")) multiplexer_1 (
    .in0(A), .in1(Mem_C), .in2(WB_C), .in3(Mem_C), .out(A_Out), .sel(and_1_out));
  Multiplexer #(.select(2), .width(32), .enable("false")) multiplexer_2 (
    .in0(B), .in1(Mem_C), .in2(WB_C), .in3(Mem_C), .out(B_Out), .sel(and_2_out));
  Comparator #(.width(4), .mode("unsigned")) comparator_1 (
    .a(A_Reg), .b(Mem_C_Reg), .eq(comparator_1_eq));  // open: gt, lt
  Comparator #(.width(4), .mode("unsigned")) comparator_2 (
    .a(B_Reg), .b(Mem_C_Reg), .eq(comparator_2_eq));  // open: gt, lt
  Comparator #(.width(4), .mode("unsigned")) comparator_3 (
    .a(Mem_C_Reg), .b(4'b0000), .eq(comparator_3_eq));  // open: gt, lt
  Comparator #(.width(4), .mode("unsigned")) comparator_4 (
    .a(Mem_C_Reg), .b(4'b1111), .eq(comparator_4_eq));  // open: gt, lt
  and and_1 (and_1_out[0], comparator_1_eq, ~or_1_out);  // AND_Gate
  and and_2 (and_2_out[0], comparator_2_eq, ~or_1_out);  // AND_Gate
  or or_1 (or_1_out, comparator_3_eq, comparator_4_eq);
  Comparator #(.width(4), .mode("unsigned")) comparator_5 (
    .a(A_Reg), .b(register_1_q), .eq(comparator_5_eq));  // open: gt, lt
  and and_3 (and_1_out[1], comparator_5_eq, ~or_2_out);  // AND_Gate
  Comparator #(.width(4), .mode("unsigned")) comparator_6 (
    .a(B_Reg), .b(register_1_q), .eq(comparator_6_eq));  // open: gt, lt
  and and_4 (and_2_out[1], comparator_6_eq, ~or_2_out);  // AND_Gate
  Comparator #(.width(4), .mode("unsigned")) comparator_7 (
    .a(register_1_q), .b(4'b0000), .eq(comparator_7_eq));  // open: gt, lt
  Comparator #(.width(4), .mode("unsigned")) comparator_8 (
    .a(register_1_q), .b(4'b1111), .eq(comparator_8_eq));  // open: gt, lt
  or or_2 (or_2_out, comparator_7_eq, comparator_8_eq);
endmodule

module ALU (
  input  [31:0] A,
  input  [31:0] B,
  input  [4:0] S,
  input  CIn,
  output [31:0] F,
  output C,
  output EQ
);

  wire and_1_out, and_2_out, C1, C2, C3, C4, C5, C6, C7, sn74181_1_aeqb, sn74181_2_aeqb, sn74181_3_aeqb,
       sn74181_4_aeqb, sn74181_5_aeqb, sn74181_6_aeqb, sn74181_7_aeqb, sn74181_8_aeqb, sn74182_1_x,
       sn74182_1_y, sn74182_2_x, sn74182_2_y, X0, X1, X2, X3, X4, X5, X6, X7, Y0, Y1, Y2, Y3, Y4, Y5, Y6, Y7;

  SN74181 sn74181_1 (
    .S(S[3:0]), .A(A[15:12]), .B(B[15:12]), .M(S[4]), .Cn(C3), .X(X3), .Y(Y3), .F(F[15:12]),
    .AeqB(sn74181_1_aeqb));  // open: Co
  and and_1 (and_1_out, sn74181_1_aeqb, sn74181_2_aeqb, sn74181_3_aeqb, sn74181_4_aeqb);
  SN74181 sn74181_2 (
    .S(S[3:0]), .A(A[11:8]), .B(B[11:8]), .M(S[4]), .Cn(C2), .X(X2), .Y(Y2), .F(F[11:8]),
    .AeqB(sn74181_2_aeqb));  // open: Co
  SN74181 sn74181_3 (
    .S(S[3:0]), .A(A[7:4]), .B(B[7:4]), .M(S[4]), .Cn(C1), .X(X1), .Y(Y1), .F(F[7:4]), .AeqB(sn74181_3_aeqb));  // open: Co
  SN74181 sn74181_4 (
    .S(S[3:0]), .A(A[3:0]), .B(B[3:0]), .M(S[4]), .Cn(CIn), .X(X0), .Y(Y0), .F(F[3:0]), .AeqB(sn74181_4_aeqb));  // open: Co
  SN74181 sn74181_5 (
    .S(S[3:0]), .A(A[31:28]), .B(B[31:28]), .M(S[4]), .Cn(C7), .X(X7), .Y(Y7), .F(F[31:28]),
    .AeqB(sn74181_5_aeqb));  // open: Co
  SN74181 sn74181_6 (
    .S(S[3:0]), .A(A[27:24]), .B(B[27:24]), .M(S[4]), .Cn(C6), .X(X6), .Y(Y6), .F(F[27:24]),
    .AeqB(sn74181_6_aeqb));  // open: Co
  SN74181 sn74181_7 (
    .S(S[3:0]), .A(A[23:20]), .B(B[23:20]), .M(S[4]), .Cn(C5), .X(X5), .Y(Y5), .F(F[23:20]),
    .AeqB(sn74181_7_aeqb));  // open: Co
  SN74181 sn74181_8 (
    .S(S[3:0]), .A(A[19:16]), .B(B[19:16]), .M(S[4]), .Cn(C4), .X(X4), .Y(Y4), .F(F[19:16]),
    .AeqB(sn74181_8_aeqb));  // open: Co
  and and_2 (and_2_out, sn74181_5_aeqb, sn74181_6_aeqb, sn74181_7_aeqb, sn74181_8_aeqb);
  and and_3 (EQ, and_1_out, and_2_out);
  SN74182 sn74182_1 (
    .X3(X7), .Y3(Y7), .X2(X6), .Y2(Y6), .X1(X5), .Y1(Y5), .X0(X4), .Y0(Y4), .Cn(C4), .X(sn74182_1_x),
    .Y(sn74182_1_y), .Coz(C7), .Coy(C6), .Cox(C5));
  SN74182 sn74182_2 (
    .X3(X3), .Y3(Y3), .X2(X2), .Y2(Y2), .X1(X1), .Y1(Y1), .X0(X0), .Y0(Y0), .Cn(CIn), .X(sn74182_2_x),
    .Y(sn74182_2_y), .Coz(C3), .Coy(C2), .Cox(C1));
  SN74182 sn74182_3 (
    .X1(sn74182_1_x), .Y1(sn74182_1_y), .X0(sn74182_2_x), .Y0(sn74182_2_y), .Cn(CIn), .Coy(C), .Cox(C4));  // open: X3, Y3, X2, Y2, X, Y, Coz
endmodule

module MEM (
  input  Clk,
  input  [31:0] F,
  input  [31:0] C,
  input  [3:0] C_Reg,
  input  [2:0] INST,
  input  [31:0] PC,
  input  [31:0] MEM_I,
  input  Reset,
  output Inhibit,
  output RD,
  output WR,
  output [31:0] ADDR,
  output [31:0] F_Out,
  output [3:0] C_Reg_Out,
  output [31:0] MEM_O
);

  wire BEQ, JLR;
  wire [0:0] or_1_out;
  wire [31:0] multiplexer_1_out;

  Decoder #(.select(3), .enable("false")) decoder_1 (
    .out2(RD), .out3(WR), .out4(JLR), .out5(BEQ), .sel(INST));  // open: out0, out1, out6, out7
  or or_1 (or_1_out[0], JLR, BEQ);
  or or_2 (Inhibit, RD, WR);
  Multiplexer #(.select(2), .width(32), .enable("false")) multiplexer_1 (
    .in0(F), .in1(PC), .in2(MEM_I), .out(multiplexer_1_out), .sel({RD, or_1_out[0]}));  // open: in3
  Register #(.width(32), .trigger("falling")) register_1 (
    .D(multiplexer_1_out), .en(1'b1), .clk(Clk), .Q(F_Out), .clr(Reset));
  Register #(.width(4), .trigger("falling")) register_2 (.D(C_Reg), .en(1'b1), .clk(Clk), .Q(C_Reg_Out), .clr(Reset));

  assign ADDR = F;
  assign MEM_O = C;

  // Other names for the same wires on the sheet: LW = RD; SW = WR
endmodule
